// Logisim project cpu.circ as structural Verilog: 1 circuit, main circuit cpu
module cpu (
  input  clk,
  input  [31:0] INSTRUCTION,
  input  [31:0] READ_DATA,
  output [31:0] WRITE_ADDRESS,
  output [31:0] PROGRAM_COUNTER,
  output [31:0] ra,
  output [31:0] sp,
  output [31:0] t0,
  output [31:0] t1,
  output [31:0] t2,
  output [31:0] s0,
  output [31:0] s1,
  output [31:0] a0,
  output [31:0] tohost,
  output [3:0] WRITE_ENABLE,
  output [31:0] WRITE_DATA
);

  wire RegWEn;
  wire [2:0] func3, ImmSel, undriven;
  wire [6:0] funct7;
  wire [24:0] INSTRUCTION_pipeline;
  wire [31:0] adder_1_out, ALU_out, complete_imm, multiplexer_1_out, PC_pipeline, rd1, rd2, WB_Data;

  Adder #(.width(32)) adder_1 (.a(PROGRAM_COUNTER), .b(32'h4), .out(adder_1_out));  // open: cin, cout
  Register #(.width(32)) PC (.D(adder_1_out), .clk(clk), .Q(PROGRAM_COUNTER));  // open: en, clr
  Register #(.width(32)) register_1 (
    .D(INSTRUCTION), .clk(clk), .Q({funct7, INSTRUCTION_pipeline[24:15], func3, INSTRUCTION_pipeline[11:0]}));  // open: en, clr
  Register #(.width(32)) register_2 (.D(PROGRAM_COUNTER), .clk(clk), .Q(PC_pipeline));  // open: en, clr
  imm_gen imm_gen_1 (
    .inst({funct7, INSTRUCTION_pipeline[24:15], func3, INSTRUCTION_pipeline[11:0]}), .ImmSel(undriven),
    .imm(complete_imm));
  // control_logic control_logic_1: pin names not known; wires that end beside it: RegWEn, ImmSel
  Multiplexer #(.enable("false"), .width(32)) multiplexer_1 (
    .in0(rd2), .in1(complete_imm), .out(multiplexer_1_out), .sel(1'b1));
  alu alu_1 (.Result(ALU_out), .A(rd1), .B(multiplexer_1_out), .ALUSel(4'b0000));
  Multiplexer #(.enable("false"), .select(2), .width(32)) multiplexer_2 (
    .in0(ALU_out), .in1(READ_DATA), .out(WB_Data), .sel(2'b00));  // open: in2, in3
  regfile regfile_1 (
    .rs1(INSTRUCTION_pipeline[19:15]), .rs2(INSTRUCTION_pipeline[24:20]), .rd(INSTRUCTION_pipeline[11:7]),
    .Write_Data(WB_Data), .RegWEn(1'b1), .clk(clk), .ra(ra), .sp(sp), .t0(t0), .t1(t1), .t2(t2), .s0(s0),
    .s1(s1), .a0(a0), .Read_Data_1(rd1), .Read_Data_2(rd2));
  // branch_comp branch_comp_1: pin names not known; wires that end beside it: rd2
  // csr csr_1: pin names not known; wires that end beside it: tohost

  // Other names for the same wires on the sheet: opcode[6:0] = INSTRUCTION_pipeline[6:0];
  //   rd[4:0] = INSTRUCTION_pipeline[11:7]; INSTRUCTION_pipeline (some bits) = {funct7, func3};
  //   rs1[4:0] = INSTRUCTION_pipeline[19:15]; rs2[4:0] = INSTRUCTION_pipeline[24:20]

  // Notes on the sheet:
  //   Output to IMEM
  //   IMEM (do **NOT** move this)
  //   Inputs from IMEM
  //   It is OK to move the PC, RegFile, ALU, MEM, Branch Comp, Imm Gen, and Control Logic to wherever is most convenient for you when constructing your CPU, and to delete this text
  //   Inputs/Outputs for testing. Do **NOT** move these.
  //   Outputs To DMEM
  //   DMEM (do **NOT** move this)
  //   Inputs From DMEM
endmodule
