// Logisim project regfile.circ as structural Verilog: 1 circuit, main circuit regfile
module regfile (
  input  [4:0] rs1,
  input  [4:0] rs2,
  input  [4:0] rd,
  input  [31:0] Write_Data,
  input  RegWEn,
  input  clk,
  output [31:0] ra,
  output [31:0] sp,
  output [31:0] t0,
  output [31:0] t1,
  output [31:0] t2,
  output [31:0] s0,
  output [31:0] s1,
  output [31:0] a0,
  output [31:0] Read_Data_1,
  output [31:0] Read_Data_2
);

  wire clock_1_out, clock_2_out, clock_3_out, clock_4_out, clock_5_out, clock_6_out, clock_7_out,
       clock_8_out, clock_9_out, clock_10_out, clock_11_out, clock_12_out, clock_13_out, clock_14_out,
       clock_15_out, clock_16_out, clock_17_out, clock_18_out, clock_19_out, clock_20_out, clock_21_out,
       clock_22_out, clock_23_out, clock_24_out, clock_25_out, clock_26_out, clock_27_out, clock_28_out,
       clock_29_out, clock_30_out, clock_31_out, x1_en, x2_en, x3_en, x4_en, x5_en, x6_en, x7_en, x8_en,
       x9_en, x10_en, x11_en, x12_en, x13_en, x14_en, x15_en, x16_en, x17_en, x18_en, x19_en, x20_en, x21_en,
       x22_en, x23_en, x24_en, x25_en, x26_en, x27_en, x28_en, x29_en, x30_en, x31_en;
  wire [31:0] x3, x4, x11, x12, x13, x14, x15, x16, x17, x18, x19, x20, x21, x22, x23, x24, x25, x26, x27,
       x28, x29, x30, x31;

  Register #(.width(32)) register_1 (.D(Write_Data), .en(x1_en), .clk(clock_1_out), .Q(ra));  // open: clr
  Clock clock_1 (.out(clock_1_out));
  Register #(.width(32)) register_2 (.D(Write_Data), .en(x9_en), .clk(clock_2_out), .Q(s1));  // open: clr
  Clock clock_2 (.out(clock_2_out));
  Register #(.width(32)) register_3 (.D(Write_Data), .en(x17_en), .clk(clock_3_out), .Q(x17));  // open: clr
  Clock clock_3 (.out(clock_3_out));
  Register #(.width(32)) register_4 (.D(Write_Data), .en(x25_en), .clk(clock_4_out), .Q(x25));  // open: clr
  Clock clock_4 (.out(clock_4_out));
  Multiplexer #(.enable("false"), .select(5), .width(32)) multiplexer_1 (
    .in0({32{1'b0}}), .in1(ra), .in2(sp), .in3(x3), .in4(x4), .in5(t0), .in6(t1), .in7(t2), .in8(s0),
    .in9(s1), .in10(a0), .in11(x11), .in12(x12), .in13(x13), .in14(x14), .in15(x15), .in16(x16), .in17(x17),
    .in18(x18), .in19(x19), .in20(x20), .in21(x21), .in22(x22), .in23(x23), .in24(x24), .in25(x25),
    .in26(x26), .in27(x27), .in28(x28), .in29(x29), .in30(x30), .in31(x31), .out(Read_Data_1), .sel(rs1));
  Register #(.width(32)) register_5 (.D(Write_Data), .en(x2_en), .clk(clock_5_out), .Q(sp));  // open: clr
  Clock clock_5 (.out(clock_5_out));
  Register #(.width(32)) register_6 (.D(Write_Data), .en(x10_en), .clk(clock_6_out), .Q(a0));  // open: clr
  Clock clock_6 (.out(clock_6_out));
  Register #(.width(32)) register_7 (.D(Write_Data), .en(x18_en), .clk(clock_7_out), .Q(x18));  // open: clr
  Clock clock_7 (.out(clock_7_out));
  Register #(.width(32)) register_8 (.D(Write_Data), .en(x26_en), .clk(clock_8_out), .Q(x26));  // open: clr
  Clock clock_8 (.out(clock_8_out));
  Register #(.width(32)) register_9 (.D(Write_Data), .en(x3_en), .clk(clock_9_out), .Q(x3));  // open: clr
  Clock clock_9 (.out(clock_9_out));
  Register #(.width(32)) register_10 (.D(Write_Data), .en(x11_en), .clk(clock_10_out), .Q(x11));  // open: clr
  Clock clock_10 (.out(clock_10_out));
  Register #(.width(32)) register_11 (.D(Write_Data), .en(x19_en), .clk(clock_11_out), .Q(x19));  // open: clr
  Clock clock_11 (.out(clock_11_out));
  Register #(.width(32)) register_12 (.D(Write_Data), .en(x27_en), .clk(clock_12_out), .Q(x27));  // open: clr
  Clock clock_12 (.out(clock_12_out));
  Register #(.width(32)) register_13 (.D(Write_Data), .en(x4_en), .clk(clock_13_out), .Q(x4));  // open: clr
  Clock clock_13 (.out(clock_13_out));
  Register #(.width(32)) register_14 (.D(Write_Data), .en(x12_en), .clk(clock_14_out), .Q(x12));  // open: clr
  Clock clock_14 (.out(clock_14_out));
  Register #(.width(32)) register_15 (.D(Write_Data), .en(x20_en), .clk(clock_15_out), .Q(x20));  // open: clr
  Clock clock_15 (.out(clock_15_out));
  Register #(.width(32)) register_16 (.D(Write_Data), .en(x28_en), .clk(clock_16_out), .Q(x28));  // open: clr
  Clock clock_16 (.out(clock_16_out));
  Register #(.width(32)) register_17 (.D(Write_Data), .en(x5_en), .clk(clock_17_out), .Q(t0));  // open: clr
  Clock clock_17 (.out(clock_17_out));
  Register #(.width(32)) register_18 (.D(Write_Data), .en(x13_en), .clk(clock_18_out), .Q(x13));  // open: clr
  Clock clock_18 (.out(clock_18_out));
  Register #(.width(32)) register_19 (.D(Write_Data), .en(x21_en), .clk(clock_19_out), .Q(x21));  // open: clr
  Clock clock_19 (.out(clock_19_out));
  Register #(.width(32)) register_20 (.D(Write_Data), .en(x29_en), .clk(clock_20_out), .Q(x29));  // open: clr
  Clock clock_20 (.out(clock_20_out));
  Register #(.width(32)) register_21 (.D(Write_Data), .en(x6_en), .clk(clock_21_out), .Q(t1));  // open: clr
  Clock clock_21 (.out(clock_21_out));
  Register #(.width(32)) register_22 (.D(Write_Data), .en(x14_en), .clk(clock_22_out), .Q(x14));  // open: clr
  Clock clock_22 (.out(clock_22_out));
  Register #(.width(32)) register_23 (.D(Write_Data), .en(x22_en), .clk(clock_23_out), .Q(x22));  // open: clr
  Clock clock_23 (.out(clock_23_out));
  Register #(.width(32)) register_24 (.D(Write_Data), .en(x30_en), .clk(clock_24_out), .Q(x30));  // open: clr
  Clock clock_24 (.out(clock_24_out));
  Multiplexer #(.enable("false"), .select(5), .width(32)) multiplexer_2 (
    .in0({32{1'b0}}), .in1(ra), .in2(sp), .in3(x3), .in4(x4), .in5(t0), .in6(t1), .in7(t2), .in8(s0),
    .in9(s1), .in10(a0), .in11(x11), .in12(x12), .in13(x13), .in14(x14), .in15(x15), .in16(x16), .in17(x17),
    .in18(x18), .in19(x19), .in20(x20), .in21(x21), .in22(x22), .in23(x23), .in24(x24), .in25(x25),
    .in26(x26), .in27(x27), .in28(x28), .in29(x29), .in30(x30), .in31(x31), .out(Read_Data_2), .sel(rs2));
  Register #(.width(32)) register_25 (.D(Write_Data), .en(x7_en), .clk(clock_25_out), .Q(t2));  // open: clr
  Clock clock_25 (.out(clock_25_out));
  Register #(.width(32)) register_26 (.D(Write_Data), .en(x15_en), .clk(clock_26_out), .Q(x15));  // open: clr
  Clock clock_26 (.out(clock_26_out));
  Register #(.width(32)) register_27 (.D(Write_Data), .en(x23_en), .clk(clock_27_out), .Q(x23));  // open: clr
  Clock clock_27 (.out(clock_27_out));
  Register #(.width(32)) register_28 (.D(Write_Data), .en(x31_en), .clk(clock_28_out), .Q(x31));  // open: clr
  Clock clock_28 (.out(clock_28_out));
  Register #(.width(32)) register_29 (.D(Write_Data), .en(x8_en), .clk(clock_29_out), .Q(s0));  // open: clr
  Clock clock_29 (.out(clock_29_out));
  Register #(.width(32)) register_30 (.D(Write_Data), .en(x16_en), .clk(clock_30_out), .Q(x16));  // open: clr
  Clock clock_30 (.out(clock_30_out));
  Register #(.width(32)) register_31 (.D(Write_Data), .en(x24_en), .clk(clock_31_out), .Q(x24));  // open: clr
  Clock clock_31 (.out(clock_31_out));
  Demultiplexer #(.enable("false"), .select(5)) demultiplexer_1 (
    .out1(x1_en), .out2(x2_en), .out3(x3_en), .out4(x4_en), .out5(x5_en), .out6(x6_en), .out7(x7_en),
    .out8(x8_en), .out9(x9_en), .out10(x10_en), .out11(x11_en), .out12(x12_en), .out13(x13_en),
    .out14(x14_en), .out15(x15_en), .out16(x16_en), .out17(x17_en), .out18(x18_en), .out19(x19_en),
    .out20(x20_en), .out21(x21_en), .out22(x22_en), .out23(x23_en), .out24(x24_en), .out25(x25_en),
    .out26(x26_en), .out27(x27_en), .out28(x28_en), .out29(x29_en), .out30(x30_en), .out31(x31_en),
    .in(RegWEn), .sel(rd));  // open: out0

  // Other names for the same wires on the sheet: read_data1[31:0] = Read_Data_1; read_data2[31:0] = Read_Data_2;
  //   read_reg1[4:0] = rs1; read_reg2[4:0] = rs2; write_en = RegWEn; write_reg[4:0] = rd; x1[31:0] = ra;
  //   x2[31:0] = sp; x5[31:0] = t0; x6[31:0] = t1; x7[31:0] = t2; x8[31:0] = s0; x9[31:0] = s1; x10[31:0] = a0

  // Notes on the sheet:
  //   INPUTS to your circuit
  //   DON'T CHANGE THE LOCATIONS OF THE INPUTS AND OUTPUTS!
  //   These are DEBUG/TEST outputs from your circuit.
  //   OUTPUTS from your circuit
endmodule
